# Fritzing sketch Wiring_diagram (saved by Fritzing 0.9.8b)
breadboards: 1

parts:
  Part1 = PocketBeagle
  J2 = Basic Servo
  J3 = Basic Servo
  J4 = Basic Servo
  J5 = Basic Servo  # not connected
  J7 = Basic Servo
  J8 = Basic Servo
  HC-SR04_Sensor_1 = HC-SR04 Ultrasonic Distance Sensor
  R1 = Resistor [tolerance=±5% resistance=220 package="0805 [SMD]"]  # not connected
  J1 = Basic Servo
  R2 = Resistor [tolerance=±5% resistance=220 package="0805 [SMD]"]  # not connected
  R3 = Resistor [tolerance=±5% resistance=220 package="0603 [SMD]"]  # not connected
  R4 = Resistor [tolerance=±5% resistance=220 package="0805 [SMD]"]  # not connected
  R5 = Resistor [tolerance=±5% resistance=220 package="0805 [SMD]"]  # not connected
  R6 = Resistor [tolerance=±5% resistance=220 package="0805 [SMD]"]  # not connected
  J9 = Basic Servo
  R7 = Resistor [tolerance=±5% resistance=220 package="0805 [SMD]"]  # not connected
  R8 = Resistor [tolerance=±5% resistance=220 package="0805 [SMD]"]  # not connected

nets:
  N1: Part1.AIN6/GPIO87, HC-SR04_Sensor_1.TRIG
  GND: Part1.GND, J2.gnd, J3.gnd, J4.gnd, J7.gnd, J8.gnd, HC-SR04_Sensor_1.GND, J1.gnd, J9.gnd
  N2: Part1.GPIO23, HC-SR04_Sensor_1.ECHO
  VCC: Part1.VOUT, J2.vcc, J3.vcc, J7.vcc, J1.vcc
  VCC_2: J4.vcc, J8.vcc, HC-SR04_Sensor_1.VCC, J9.vcc
